# Fritzing sketch TMP36-LED (saved by Fritzing 0.9.3b)
breadboards: 1

parts:
  Part19 = Tessel 2
  U1 = TMP36 [package=to-92-kit]
  LED2 = LED - 5mm [color="Red (633nm)" package="5 mm [THT]"]
  R2 = Resistor [tolerance=±5% resistance=100 package="0402 [SMD]"]

nets:
  GND: Part19.GND, U1.GND, R2.Pin_1
  3V3: Part19.3V3, U1.VCC
  N1: Part19.4, U1.VOUT
  N2: Part19.5, LED2.anode
  N3: LED2.cathode, R2.Pin_0

custom parts:
  Tessel 2: Draft version of Tessel 2
