# Fritzing sketch button (saved by Fritzing 0.9.3b)
breadboards: 1

parts:
  LED1 = LED - 5mm [color="Red (633nm)" package="5 mm [THT]"]
  R1 = Resistor [tolerance=±5% resistance=100 package="0402 [SMD]"]
  S1 = Pushbutton [package="[THT]"]
  R2 = Resistor [tolerance=±5% resistance=10k package="0402 [SMD]"]
  Part1 = Arduino Uno (Rev3)

nets:
  N1: LED1.cathode, R1.Pin_1
  N2: LED1.anode, Part1.D11_PWM/MOSI
  N3: R1.Pin_0, R2.Pin_1, Part1.GND
  N4: S1.Pin_1, S1.Pin_2, R2.Pin_0, Part1.D2
  N5: S1.Pin_3, S1.Pin_4, Part1.5V
