# Fritzing sketch buttonT2 (saved by Fritzing 0.9.3b)
breadboards: 1

parts:
  Part19 = Tessel 2
  LED1 = LED - 5mm [color="Red (633nm)" package="5 mm [THT]"]
  R1 = Resistor [tolerance=±5% resistance=10k package="0402 [SMD]"]
  S1 = Pushbutton [package="[THT]"]
  R2 = Resistor [tolerance=±5% resistance=100 package="0402 [SMD]"]

nets:
  N1: Part19.GND, R1.Pin_1, R2.Pin_0
  N2: Part19.3V3, S1.Pin_3, S1.Pin_4
  N3: Part19.4, R1.Pin_0, S1.Pin_1, S1.Pin_2
  N4: Part19.5, LED1.anode
  N5: LED1.cathode, R2.Pin_1

custom parts:
  Tessel 2: Draft version of Tessel 2
