# Fritzing sketch ledT2 (saved by Fritzing 0.9.3b)
breadboards: 1

parts:
  Part19 = Tessel 2
  LED1 = LED - 5mm [color="Red (633nm)" package="5 mm [THT]"]
  R1 = Resistor [tolerance=±5% resistance=100 package="0402 [SMD]"]

nets:
  N1: Part19.GND, R1.Pin_0
  N2: Part19.5, LED1.anode
  N3: LED1.cathode, R1.Pin_1

custom parts:
  Tessel 2: Draft version of Tessel 2
