# Fritzing sketch potentiometerT2 (saved by Fritzing 0.9.3b)
breadboards: 1

parts:
  Part19 = Tessel 2
  LED1 = LED - 5mm [color="Red (633nm)" package="5 mm [THT]"]
  R1 = Resistor [tolerance=±5% resistance=100 package="0402 [SMD]"]
  R3 = TRIMPOT [package=trimpot_pth_s3_lock]

nets:
  N1: Part19.GND, R1.Pin_0, R3.CW
  N2: Part19.3V3, R3.CCW
  N3: Part19.4, R3.WIPER
  N4: Part19.5, LED1.anode
  N5: LED1.cathode, R1.Pin_1

custom parts:
  Tessel 2: Draft version of Tessel 2
