# Fritzing sketch servo (saved by Fritzing 0.9.3b)
breadboards: 1

parts:
  Part1 = Arduino Uno (Rev3)
  J1 = Basic Servo
  VCC3 = Battery
  VCC2 = Battery

nets:
  N1: Part1.D11_PWM/MOSI, J1.pulse
  GND: Part1.GND, J1.gnd, VCC3.-
  N2: J1.vcc, VCC2.+
