# Fritzing sketch servoT2 (saved by Fritzing 0.9.3b)
breadboards: 1

parts:
  J1 = Basic Servo
  VCC3 = Battery
  VCC2 = Battery
  Part20 = Tessel 2

nets:
  GND: J1.gnd, VCC3.-, Part20.GND
  N1: J1.vcc, VCC2.+

custom parts:
  Tessel 2: Draft version of Tessel 2
