# Fritzing sketch servosT2 (saved by Fritzing 0.9.3b)
breadboards: 1

parts:
  J1 = Basic Servo
  VCC3 = Battery
  VCC2 = Battery
  Part20 = Tessel 2
  J2 = Basic Servo

nets:
  GND: J1.gnd, VCC3.-, Part20.GND, J2.gnd
  VCC: J1.vcc, VCC2.+, J2.vcc

custom parts:
  Tessel 2: Draft version of Tessel 2
