# Fritzing sketch temperatureT2 (saved by Fritzing 0.9.3b)
breadboards: 1

parts:
  Part19 = Tessel 2
  U1 = TMP36 [package=to-92-kit]

nets:
  GND: Part19.GND, U1.GND
  3V3: Part19.3V3, U1.VCC
  N1: Part19.4, U1.VOUT

custom parts:
  Tessel 2: Draft version of Tessel 2
